// Logisim project task1.circ as structural Verilog: 1 circuit, main circuit main
module main (
  input  in_1,
  input  in_2,
  input  in_3
);

  wire and_1_out, and_2_out, and_3_out, and_4_out, and_5_out, and_6_out, and_7_out, and_8_out, and_9_out,
       clock_1_out, d_ff_1_q, d_ff_2_q, d_ff_3_q, nand_1_out, or_1_out;

  Clock clock_1 (.out(clock_1_out));
  or or_1 (or_1_out, in_1, in_2);
  and and_1 (and_1_out, or_1_out, nand_1_out);
  and and_2 (and_2_out, d_ff_1_q, nand_1_out);
  and and_3 (and_3_out, d_ff_2_q, nand_1_out);
  D_Flip_Flop d_ff_1 (.clk(clock_1_out), .D(and_1_out), .Q(d_ff_1_q));  // open: Qn, preset, en, reset
  D_Flip_Flop d_ff_2 (.clk(clock_1_out), .D(and_2_out), .Q(d_ff_2_q));  // open: Qn, preset, en, reset
  D_Flip_Flop d_ff_3 (.clk(clock_1_out), .D(and_3_out), .Q(d_ff_3_q));  // open: Qn, preset, en, reset
  nand nand_1 (nand_1_out, d_ff_1_q, d_ff_2_q, d_ff_3_q);
  and and_4 (and_4_out, in_1, d_ff_1_q);
  and and_5 (and_5_out, in_1, d_ff_2_q);
  and and_6 (and_6_out, in_1, d_ff_3_q);
  LED led_1 (.in(and_5_out));
  LED led_2 (.in(and_6_out));
  LED led_3 (.in(and_4_out));
  LED led_4 (.in(and_9_out));
  and and_7 (and_7_out, in_2, d_ff_1_q);
  and and_8 (and_8_out, in_2, d_ff_2_q);
  and and_9 (and_9_out, in_2, d_ff_3_q);
  LED led_5 (.in(and_8_out));
  LED led_6 (.in(and_7_out));
endmodule
